// Logisim project Digital_Access_Card_Verification_System (1).circ as structural Verilog: 1 circuit, main circuit main
// Digital Access Card Verification System
module main (
  input  A__Card_ID,
  input  B__Card_ID,
  input  C__Parity,
  input  D__Parity,
  output Access__Granted_1,
  output Alarm__Denied_1
);

  wire ID_Match_out, Parity_Check_out;

  // AND_Gate ID_Match has open pins: out=ID_Match_out
  // XOR_Gate Parity_Check has open pins: out=Parity_Check_out
  // OR_Gate Access has open pins: out=Access__Granted_1
  LED Granted (.in(Access__Granted_1));
  not Alarm (Alarm__Denied_1, Access__Granted_1);
  LED Denied___Alarm (.in(Alarm__Denied_1));

  // Notes on the sheet:
  //   A,B = Card ID bits | C,D = Parity bits | Green LED = Access Granted | Red LED = Alarm
  //   Based on Project: Dual Validation with ID Match (AND) + Parity Error Detection (XOR)
  //   Access = (A · B) + (C ⊕ D)
  //   Digital Access Card Verification System - Pure Combinational Logic
endmodule
